// Logisim project 3x3Adder_Albert.circ as structural Verilog: 1 circuit, main circuit main
module main (
  input  x2,
  input  x1,
  input  x0,
  input  y2,
  input  y1,
  input  y0,
  output c,
  output z2,
  output z1,
  output z0
);

  wire and_1_out, and_2_out, and_3_out, and_4_out, and_5_out, and_6_out, and_7_out, and_8_out, and_9_out,
       and_10_out, and_11_out, and_12_out, and_13_out, and_14_out, and_15_out, and_16_out, and_17_out,
       and_18_out, and_19_out, and_20_out, and_21_out, and_22_out, and_23_out, and_24_out, and_25_out,
       and_26_out, and_27_out, and_28_out, and_29_out, and_30_out, and_31_out, and_32_out, and_33_out,
       and_34_out, and_35_out, and_36_out, and_37_out, and_38_out, and_39_out, and_40_out, and_41_out,
       and_42_out, and_43_out, and_44_out, and_45_out, and_46_out, and_47_out, and_48_out, and_49_out,
       and_50_out, and_51_out, and_52_out, and_53_out, and_54_out, and_55_out, and_56_out, and_57_out,
       and_58_out, and_59_out, and_60_out, and_61_out, and_62_out, and_63_out, and_64_out, and_65_out,
       and_66_out, and_67_out, and_68_out, or_1_out;

  and and_1 (and_1_out, x0, y0);
  or or_1 (or_1_out, y0, x0);
  and and_2 (and_2_out, y0, x0, ~x1, ~y1);  // AND_Gate
  and and_3 (and_3_out, y1, ~x1, ~y0, ~y0);  // AND_Gate
  and and_4 (and_4_out, ~y1, x1, ~y0, ~x0);  // AND_Gate
  and and_5 (and_5_out, x1, y1, y0, x0);
  and and_6 (and_6_out, ~x1, y1, ~x0, y0);  // AND_Gate
  and and_7 (and_7_out, x1, y0, ~y1, ~x0);  // AND_Gate
  and and_8 (and_8_out, x0, ~y0, x1, ~y1);  // AND_Gate
  and and_9 (and_9_out, x0, y0, x1, ~y1, y2, x2);  // AND_Gate
  and and_10 (and_10_out, x2, y2, y1, ~x1, y0, x0);  // AND_Gate
  and and_11 (and_11_out, ~x0, y2, ~y0, ~x1, ~y1, ~x2);  // AND_Gate
  and and_12 (and_12_out, x2, ~y1, ~x1, ~y0, ~x0, ~y2);  // AND_Gate
  and and_13 (and_13_out, ~y2, ~x2, x0, y0, x1, y1);  // AND_Gate
  and and_14 (and_14_out, ~y2, ~y1, x1, ~x2, y0, x0);  // AND_Gate
  and and_15 (and_15_out, ~y2, y1, ~x1, ~x2, y0, x0);  // AND_Gate
  and and_16 (and_16_out, y2, y1, x1, x2, y0, x0);
  and and_17 (and_17_out, y2, y1, x1, x2, ~y0, x0);  // AND_Gate
  and and_18 (and_18_out, y2, y1, x1, x2, y0, ~x0);  // AND_Gate
  and and_19 (and_19_out, ~y2, y1, x1, ~x2, ~y0, ~x0);  // AND_Gate
  and and_20 (and_20_out, ~y2, y1, x1, ~x2, ~y0, x0);  // AND_Gate
  and and_21 (and_21_out, ~y2, y1, x1, ~x2, y0, ~x0);  // AND_Gate
  and and_22 (and_22_out, y2, ~y1, x1, ~x2, ~y0, ~x0);  // AND_Gate
  and and_23 (and_23_out, y2, ~y1, x1, ~x2, y0, ~x0);  // AND_Gate
  and and_24 (and_24_out, ~y2, ~y1, x1, x2, y0, ~x0);  // AND_Gate
  and and_25 (and_25_out, ~y2, y1, ~x1, x2, ~y0, x0);  // AND_Gate
  and and_26 (and_26_out, y2, y1, ~x1, ~x2, ~y0, x0);  // AND_Gate
  and and_27 (and_27_out, y2, y1, ~x1, ~x2, y0, ~x0);  // AND_Gate
  and and_28 (and_28_out, ~y2, ~y1, x1, x2, ~y0, x0);  // AND_Gate
  and and_29 (and_29_out, ~y2, ~y1, ~x1, x2, ~y0, x0);  // AND_Gate
  and and_30 (and_30_out, y2, ~y1, ~x1, ~x2, ~y0, x0);  // AND_Gate
  and and_31 (and_31_out, y2, ~y1, ~x1, ~x2, y0, ~x0);  // AND_Gate
  and and_32 (and_32_out, ~y2, ~y1, ~x1, x2, y0, ~x0);  // AND_Gate
  and and_33 (and_33_out, y2, ~y1, ~x1, ~x2, y0, x0);  // AND_Gate
  and and_34 (and_34_out, ~y2, ~y1, ~x1, x2, y0, x0);  // AND_Gate
  and and_35 (and_35_out, y2, y1, ~x1, ~x2, ~y0, ~x0);  // AND_Gate
  and and_36 (and_36_out, y2, ~y1, x1, ~x2, ~y0, x0);  // AND_Gate
  and and_37 (and_37_out, ~y2, y1, ~x1, x2, ~y0, ~x0);  // AND_Gate
  and and_38 (and_38_out, ~y2, y1, ~x1, x2, y0, ~x0);  // AND_Gate
  and and_39 (and_39_out, ~y2, ~y1, x1, x2, ~y0, ~x0);  // AND_Gate
  and and_40 (and_40_out, y2, y1, x1, x2, ~y0, ~x0);  // AND_Gate
  and and_41 (and_41_out, y2, y1, ~x1, ~x2, y0, x0);  // AND_Gate
  and and_42 (and_42_out, y2, y1, x1, ~x2, ~y0, ~x0);  // AND_Gate
  and and_43 (and_43_out, y2, y1, x1, ~x2, y0, ~x0);  // AND_Gate
  and and_44 (and_44_out, y2, ~y1, x1, ~x2, y0, x0);  // AND_Gate
  and and_45 (and_45_out, y2, y1, x1, ~x2, ~y0, x0);  // AND_Gate
  and and_46 (and_46_out, y2, y1, x1, ~x2, y0, x0);  // AND_Gate
  and and_47 (and_47_out, y2, ~y1, ~x1, x2, ~y0, ~x0);  // AND_Gate
  and and_48 (and_48_out, y2, ~y1, ~x1, x2, y0, ~x0);  // AND_Gate
  and and_49 (and_49_out, y2, y1, ~x1, x2, ~y0, ~x0);  // AND_Gate
  and and_50 (and_50_out, y2, y1, ~x1, x2, y0, ~x0);  // AND_Gate
  and and_51 (and_51_out, ~y2, y1, ~x1, x2, y0, x0);  // AND_Gate
  and and_52 (and_52_out, y2, ~y1, ~x1, x2, ~y0, x0);  // AND_Gate
  and and_53 (and_53_out, y2, ~y1, ~x1, x2, y0, x0);  // AND_Gate
  and and_54 (and_54_out, y2, y1, ~x1, x2, ~y0, x0);  // AND_Gate
  and and_55 (and_55_out, y2, y1, ~x1, x2, y0, x0);  // AND_Gate
  and and_56 (and_56_out, ~y2, y1, x1, x2, ~y0, ~x0);  // AND_Gate
  and and_57 (and_57_out, ~y2, y1, x1, x2, y0, ~x0);  // AND_Gate
  and and_58 (and_58_out, y2, ~y1, x1, x2, ~y0, ~x0);  // AND_Gate
  and and_59 (and_59_out, y2, ~y1, x1, x2, y0, ~x0);  // AND_Gate
  and and_60 (and_60_out, y2, y1, x1, x2, ~y0, ~x0);  // AND_Gate
  and and_61 (and_61_out, y2, y1, x1, x2, y0, ~x0);  // AND_Gate
  and and_62 (and_62_out, ~y2, ~y1, x1, x2, y0, x0);  // AND_Gate
  and and_63 (and_63_out, ~y2, y1, x1, x2, ~y0, x0);  // AND_Gate
  and and_64 (and_64_out, ~y2, y1, x1, x2, y0, x0);  // AND_Gate
  and and_65 (and_65_out, y2, ~y1, x1, x2, ~y0, x0);  // AND_Gate
  and and_66 (and_66_out, y2, ~y1, x1, x2, y0, x0);  // AND_Gate
  and and_67 (and_67_out, y2, y1, x1, x2, ~y0, x0);  // AND_Gate
  and and_68 (and_68_out, y2, y1, x1, x2, y0, x0);
  and and_69 (z0, ~and_1_out, or_1_out);  // AND_Gate
  or or_2 (z1, and_2_out, and_3_out, and_4_out, and_7_out, and_5_out, and_8_out, and_6_out);
  or or_3 (c, and_41_out, and_42_out, and_43_out, and_44_out, and_45_out, and_46_out, and_47_out, and_48_out, and_49_out, and_50_out, and_51_out, and_52_out, and_53_out, and_54_out, and_55_out, and_56_out, and_57_out, and_58_out, and_59_out, and_60_out, and_61_out, and_62_out, and_63_out, and_64_out, and_65_out, and_66_out, and_67_out, and_68_out);
  or or_4 (z2, and_38_out, and_39_out, and_40_out, and_12_out, and_29_out, and_28_out, and_27_out, and_23_out, and_22_out, and_21_out, and_20_out, and_19_out, and_18_out, and_9_out, and_10_out, and_11_out, and_13_out, and_14_out, and_15_out, and_16_out, and_17_out, and_24_out, and_25_out, and_30_out, and_26_out, and_31_out, and_32_out, and_33_out, and_34_out, and_35_out, and_36_out, and_37_out);
endmodule
