// Logisim project 3x3Adder_Matthew.circ as structural Verilog: 1 circuit, main circuit main
module main (
  input  x0,
  input  x1,
  input  x2,
  input  y0,
  input  y1,
  input  y2,
  output c,
  output z2,
  output z1,
  output z0
);

  wire and_1_out, and_2_out, and_3_out, and_4_out, and_5_out, and_6_out, and_7_out, and_8_out, and_9_out,
       and_10_out, and_11_out, and_12_out, and_13_out, and_14_out;

  and and_1 (and_1_out, x0, y0);
  and and_2 (and_2_out, x0, ~y0, x1);  // AND_Gate
  and and_3 (and_3_out, ~x0, y0, x1);  // AND_Gate
  and and_4 (and_4_out, x0, y0, x1, y1, x2, y2);
  and and_5 (and_5_out, ~x0, y0, ~x1, y1, x2, y2);  // AND_Gate
  and and_6 (and_6_out, ~x1, y1);  // AND_Gate
  and and_7 (and_7_out, ~x0, ~y0);  // AND_Gate
  and and_8 (and_8_out, y0, x0);
  and and_9 (and_9_out, x1, ~y1);  // AND_Gate
  and and_10 (and_10_out, ~x1, y1);  // AND_Gate
  and and_11 (and_11_out, ~x1, ~y1, x2, y2);  // AND_Gate
  and and_12 (and_12_out, y1, x1, x2, y2);
  and and_13 (and_13_out, x2, ~y2);  // AND_Gate
  and and_14 (and_14_out, ~x2, y2);  // AND_Gate
  or or_1 (c, and_1_out, and_2_out, and_3_out, and_4_out, and_5_out);
  or or_2 (z2, and_6_out, and_7_out, and_8_out);
  or or_3 (z1, and_9_out, and_10_out, and_11_out, and_12_out);
  or or_4 (z0, and_13_out, and_14_out);
endmodule
