// Logisim project 3x3Subtractor_ALbert.circ as structural Verilog: 1 circuit, main circuit main
module main (
  input  x2,
  input  x1,
  input  x0,
  input  y2,
  input  y1,
  input  y0,
  output c,
  output x2_2,
  output z1,
  output z0
);

  wire and_1_out, and_2_out, and_3_out, and_4_out, and_5_out, and_6_out, and_7_out, and_8_out, and_9_out,
       and_10_out, and_11_out, and_12_out, and_13_out, and_14_out, and_15_out, and_16_out, and_17_out,
       and_18_out, and_19_out, and_20_out, and_21_out, and_22_out, and_23_out, and_24_out, and_25_out,
       and_26_out, and_27_out, and_28_out, and_29_out, and_30_out, and_31_out, and_32_out, and_33_out,
       and_34_out, and_35_out, and_36_out, and_37_out, and_38_out, and_39_out, and_40_out, and_41_out,
       and_42_out, and_43_out, and_44_out, and_45_out, and_46_out, and_47_out, and_48_out, and_49_out,
       and_50_out, and_51_out, and_52_out, and_53_out, and_54_out, and_55_out, and_56_out, and_57_out,
       and_58_out, and_59_out, and_60_out, and_61_out, and_62_out, and_63_out, and_64_out, and_65_out,
       and_66_out, and_67_out, and_68_out, and_69_out, and_70_out, and_71_out, and_72_out, and_73_out,
       and_74_out, and_75_out, and_76_out, and_77_out, and_78_out, and_79_out, and_80_out, and_81_out,
       and_82_out, and_83_out, and_84_out, and_85_out, and_86_out, and_87_out, and_88_out, and_89_out,
       and_90_out, and_91_out, and_92_out, and_93_out, and_94_out, and_95_out, and_96_out, and_97_out,
       and_98_out, and_99_out, and_100_out, and_101_out, and_102_out, and_103_out, and_104_out;

  and and_1 (and_1_out, ~x2, ~y2, ~x1, ~y1, ~x0, y0);  // AND_Gate
  and and_2 (and_2_out, ~x2, ~y2, ~x1, y1, ~x0, y0);  // AND_Gate
  and and_3 (and_3_out, ~x2, y2, ~x1, ~y1, ~x0, y0);  // AND_Gate
  and and_4 (and_4_out, ~x2, y2, ~x1, y1, ~x0, y0);  // AND_Gate
  and and_5 (and_5_out, ~x2, ~y2, ~x1, ~y1, x0, ~y0);  // AND_Gate
  and and_6 (and_6_out, ~x2, ~y2, ~x1, y1, x0, ~y0);  // AND_Gate
  and and_7 (and_7_out, ~x2, y2, ~x1, ~y1, x0, ~y0);  // AND_Gate
  and and_8 (and_8_out, ~x2, y2, ~x1, y1, x0, ~y0);  // AND_Gate
  and and_9 (and_9_out, ~x2, ~y2, x1, ~y1, ~x0, y0);  // AND_Gate
  and and_10 (and_10_out, ~x2, ~y2, x1, y1, ~x0, y0);  // AND_Gate
  and and_11 (and_11_out, ~x2, y2, x1, ~y1, ~x0, y0);  // AND_Gate
  and and_12 (and_12_out, ~x2, y2, x1, y1, ~x0, y0);  // AND_Gate
  and and_13 (and_13_out, ~x2, ~y2, x1, ~y1, x0, ~y0);  // AND_Gate
  and and_14 (and_14_out, ~x2, ~y2, x1, y1, x0, ~y0);  // AND_Gate
  and and_15 (and_15_out, ~x2, y2, x1, ~y1, x0, ~y0);  // AND_Gate
  and and_16 (and_16_out, ~x2, y2, x1, y1, x0, ~y0);  // AND_Gate
  and and_17 (and_17_out, x2, ~y2, ~x1, ~y1, ~x0, y0);  // AND_Gate
  and and_18 (and_18_out, x2, ~y2, ~x1, y1, ~x0, y0);  // AND_Gate
  and and_19 (and_19_out, x2, y2, ~x1, ~y1, ~x0, y0);  // AND_Gate
  and and_20 (and_20_out, x2, y2, ~x1, y1, ~x0, y0);  // AND_Gate
  and and_21 (and_21_out, x2, ~y2, ~x1, ~y1, x0, ~y0);  // AND_Gate
  and and_22 (and_22_out, x2, ~y2, ~x1, y1, x0, ~y0);  // AND_Gate
  and and_23 (and_23_out, x2, y2, ~x1, ~y1, x0, ~y0);  // AND_Gate
  and and_24 (and_24_out, x2, y2, ~x1, y1, x0, ~y0);  // AND_Gate
  and and_25 (and_25_out, x2, ~y2, x1, ~y1, ~x0, y0);  // AND_Gate
  and and_26 (and_26_out, x2, ~y2, x1, y1, ~x0, y0);  // AND_Gate
  and and_27 (and_27_out, x2, y2, x1, ~y1, ~x0, y0);  // AND_Gate
  and and_28 (and_28_out, x2, y2, x1, y1, ~x0, y0);  // AND_Gate
  and and_29 (and_29_out, x2, ~y2, x1, ~y1, x0, ~y0);  // AND_Gate
  and and_30 (and_30_out, x2, ~y2, x1, y1, x0, ~y0);  // AND_Gate
  and and_31 (and_31_out, x2, y2, x1, ~y1, x0, ~y0);  // AND_Gate
  and and_32 (and_32_out, x2, y2, x1, y1, x0, ~y0);  // AND_Gate
  and and_33 (and_33_out, ~x2, ~y2, ~x1, y1, ~x0, ~y0);  // AND_Gate
  and and_34 (and_34_out, ~x2, ~y2, ~x1, y1, ~x0, y0);  // AND_Gate
  and and_35 (and_35_out, ~x2, y2, ~x1, y1, ~x0, ~y0);  // AND_Gate
  and and_36 (and_36_out, ~x2, y2, ~x1, y1, ~x0, y0);  // AND_Gate
  and and_37 (and_37_out, ~x2, ~y2, ~x1, y1, x0, y0);  // AND_Gate
  and and_38 (and_38_out, ~x2, y2, ~x1, ~y1, x0, ~y0);  // AND_Gate
  and and_39 (and_39_out, ~x2, y2, ~x1, y1, x0, y0);  // AND_Gate
  and and_40 (and_40_out, ~x2, ~y2, x1, ~y1, ~x0, ~y0);  // AND_Gate
  and and_41 (and_41_out, ~x2, y2, x1, ~y1, ~x0, ~y0);  // AND_Gate
  and and_42 (and_42_out, ~x2, y2, x1, ~y1, ~x0, y0);  // AND_Gate
  and and_43 (and_43_out, ~x2, ~y2, x1, ~y1, x0, ~y0);  // AND_Gate
  and and_44 (and_44_out, ~x2, ~y2, x1, ~y1, x0, y0);  // AND_Gate
  and and_45 (and_45_out, ~x2, y2, x1, ~y1, x0, y0);  // AND_Gate
  and and_46 (and_46_out, ~x2, y2, x1, y1, x0, ~y0);  // AND_Gate
  and and_47 (and_47_out, x2, ~y2, ~x1, ~y1, ~x0, y0);  // AND_Gate
  and and_48 (and_48_out, x2, ~y2, ~x1, y1, ~x0, ~y0);  // AND_Gate
  and and_49 (and_49_out, x2, y2, ~x1, y1, ~x0, ~y0);  // AND_Gate
  and and_50 (and_50_out, x2, y2, ~x1, y1, ~x0, y0);  // AND_Gate
  and and_51 (and_51_out, x2, ~y2, ~x1, y1, x0, ~y0);  // AND_Gate
  and and_52 (and_52_out, x2, ~y2, ~x1, y1, x0, y0);  // AND_Gate
  and and_53 (and_53_out, x2, y2, ~x1, y1, x0, y0);  // AND_Gate
  and and_54 (and_54_out, x2, ~y2, x1, ~y1, ~x0, ~y0);  // AND_Gate
  and and_55 (and_55_out, x2, ~y2, x1, y1, ~x0, y0);  // AND_Gate
  and and_56 (and_56_out, x2, y2, x1, ~y1, ~x0, ~y0);  // AND_Gate
  and and_57 (and_57_out, x2, ~y2, x1, ~y1, x0, ~y0);  // AND_Gate
  and and_58 (and_58_out, x2, ~y2, x1, ~y1, x0, y0);  // AND_Gate
  and and_59 (and_59_out, x2, y2, x1, ~y1, x0, ~y0);  // AND_Gate
  and and_60 (and_60_out, x2, y2, x1, ~y1, x0, y0);  // AND_Gate
  and and_61 (and_61_out, ~x2, y2, ~x1, ~y1, ~x0, ~y0);  // AND_Gate
  and and_62 (and_62_out, ~x2, y2, ~x1, ~y1, ~x0, y0);  // AND_Gate
  and and_63 (and_63_out, ~x2, y2, ~x1, y1, ~x0, ~y0);  // AND_Gate
  and and_64 (and_64_out, ~x2, y2, ~x1, y1, ~x0, y0);  // AND_Gate
  and and_65 (and_65_out, ~x2, y2, ~x1, ~y1, x0, y0);  // AND_Gate
  and and_66 (and_66_out, ~x2, y2, ~x1, y1, x0, ~y0);  // AND_Gate
  and and_67 (and_67_out, ~x2, y2, ~x1, y1, x0, y0);  // AND_Gate
  and and_68 (and_68_out, ~x2, y2, x1, y1, ~x0, ~y0);  // AND_Gate
  and and_69 (and_69_out, ~x2, y2, x1, y1, ~x0, y0);  // AND_Gate
  and and_70 (and_70_out, ~x2, y2, x1, y1, x0, y0);  // AND_Gate
  and and_71 (and_71_out, x2, ~y2, ~x1, ~y1, ~x0, ~y0);  // AND_Gate
  and and_72 (and_72_out, x2, ~y2, ~x1, ~y1, x0, ~y0);  // AND_Gate
  and and_73 (and_73_out, x2, ~y2, ~x1, ~y1, x0, y0);  // AND_Gate
  and and_74 (and_74_out, x2, ~y2, x1, ~y1, ~x0, ~y0);  // AND_Gate
  and and_75 (and_75_out, x2, ~y2, x1, ~y1, ~x0, y0);  // AND_Gate
  and and_76 (and_76_out, x2, ~y2, x1, y1, ~x0, ~y0);  // AND_Gate
  and and_77 (and_77_out, x2, ~y2, x1, ~y1, x0, ~y0);  // AND_Gate
  and and_78 (and_78_out, x2, ~y2, x1, ~y1, x0, y0);  // AND_Gate
  and and_79 (and_79_out, x2, ~y2, x1, y1, x0, ~y0);  // AND_Gate
  and and_80 (and_80_out, x2, ~y2, x1, y1, x0, y0);  // AND_Gate
  and and_81 (and_81_out, ~x2, ~y2, ~x1, ~y1, ~x0, y0);  // AND_Gate
  and and_82 (and_82_out, ~x2, ~y2, ~x1, y1, ~x0, ~y0);  // AND_Gate
  and and_83 (and_83_out, ~x2, ~y2, ~x1, y1, ~x0, y0);  // AND_Gate
  and and_84 (and_84_out, ~x2, y2, ~x1, ~y1, ~x0, ~y0);  // AND_Gate
  and and_85 (and_85_out, ~x2, y2, ~x1, ~y1, ~x0, y0);  // AND_Gate
  and and_86 (and_86_out, ~x2, y2, ~x1, y1, ~x0, ~y0);  // AND_Gate
  and and_87 (and_87_out, ~x2, y2, ~x1, y1, ~x0, y0);  // AND_Gate
  and and_88 (and_88_out, ~x2, ~y2, ~x1, y1, x0, ~y0);  // AND_Gate
  and and_89 (and_89_out, ~x2, ~y2, ~x1, y1, x0, y0);  // AND_Gate
  and and_90 (and_90_out, ~x2, y2, ~x1, ~y1, x0, ~y0);  // AND_Gate
  and and_91 (and_91_out, ~x2, y2, ~x1, ~y1, x0, y0);  // AND_Gate
  and and_92 (and_92_out, ~x2, y2, ~x1, y1, x0, ~y0);  // AND_Gate
  and and_93 (and_93_out, ~x2, y2, ~x1, y1, x0, y0);  // AND_Gate
  and and_94 (and_94_out, ~x2, ~y2, x1, y1, ~x0, y0);  // AND_Gate
  and and_95 (and_95_out, ~x2, y2, x1, ~y1, ~x0, ~y0);  // AND_Gate
  and and_96 (and_96_out, ~x2, y2, x1, ~y1, ~x0, y0);  // AND_Gate
  and and_97 (and_97_out, ~x2, y2, x1, y1, ~x0, ~y0);  // AND_Gate
  and and_98 (and_98_out, ~x2, y2, x1, y1, ~x0, y0);  // AND_Gate
  and and_99 (and_99_out, ~x2, y2, x1, ~y1, x0, ~y0);  // AND_Gate
  and and_100 (and_100_out, x2, y2, ~x1, ~y1, ~x0, y0);  // AND_Gate
  and and_101 (and_101_out, x2, y2, ~x1, y1, ~x0, ~y0);  // AND_Gate
  and and_102 (and_102_out, x2, y2, ~x1, y1, ~x0, y0);  // AND_Gate
  and and_103 (and_103_out, x2, y2, ~x1, y1, x0, ~y0);  // AND_Gate
  and and_104 (and_104_out, x2, y2, x1, y1, ~x0, y0);  // AND_Gate
  or or_1 (z0, and_1_out, and_2_out, and_3_out, and_4_out, and_5_out, and_6_out, and_7_out, and_8_out, and_9_out, and_10_out, and_11_out, and_12_out, and_13_out, and_14_out, and_15_out, and_16_out, and_17_out, and_18_out, and_19_out, and_20_out, and_21_out, and_22_out, and_23_out, and_24_out, and_25_out, and_26_out, and_27_out, and_28_out, and_29_out, and_30_out, and_31_out, and_32_out);
  or or_2 (z1, and_33_out, and_34_out, and_35_out, and_36_out, and_37_out, and_38_out, and_39_out, and_40_out, and_41_out, and_42_out, and_43_out, and_44_out, and_45_out, and_46_out, and_47_out, and_48_out, and_49_out, and_50_out, and_51_out, and_52_out, and_53_out, and_54_out, and_55_out, and_56_out, and_57_out, and_58_out, and_59_out, and_60_out);
  or or_3 (x2_2, and_61_out, and_62_out, and_63_out, and_64_out, and_65_out, and_66_out, and_67_out, and_68_out, and_69_out, and_70_out, and_71_out, and_72_out, and_73_out, and_74_out, and_75_out, and_76_out, and_77_out, and_78_out, and_79_out, and_80_out);
  or or_4 (c, and_81_out, and_82_out, and_83_out, and_84_out, and_85_out, and_86_out, and_87_out, and_88_out, and_89_out, and_90_out, and_91_out, and_92_out, and_93_out, and_94_out, and_95_out, and_96_out, and_97_out, and_98_out, and_99_out, and_100_out, and_101_out, and_102_out, and_103_out, and_104_out);
endmodule
