// Logisim project musicBox.circ as structural Verilog: 1 circuit, main circuit main
module main (
  input  in_1
);

  wire clock_1_out, or_1_out;
  wire [2:0] adder_1_out, register_1_q;
  wire [7:0] rom_1_data;

  Register #(.width(3)) register_1 (.D(adder_1_out), .en(1'b1), .Q(register_1_q), .clk(clock_1_out), .clr(or_1_out));
  Clock clock_1 (.out(clock_1_out));
  or or_1 (or_1_out, in_1, rom_1_data[7]);
  Adder #(.width(3)) adder_1 (.a(3'b000), .b(register_1_q), .out(adder_1_out), .cin(1'b1));  // open: cout
  ROM #(.addrWidth(3)) rom_1 (.addr(register_1_q), .data(rom_1_data));  // open: sel
  _7_Segment_Display u_7_segment_display_1 (
    .g(rom_1_data[6]), .f(rom_1_data[5]), .a(rom_1_data[0]), .b(rom_1_data[1]), .e(rom_1_data[4]),
    .d(rom_1_data[3]), .c(rom_1_data[2]));  // open: dp

  // Notes on the sheet:
  //   contents of rom_1 (hex, n*v repeats v):
  //   77 7c 39 5e 79 71 80
endmodule
